// Logisim project Demultiplexer.circ as structural Verilog: 1 circuit, main circuit main
module main (
  input  Intput1,
  input  Input_2,
  input  D
);

  wire and_1_out, and_2_out, and_3_out, and_4_out, not_1_out, not_2_out;

  not not_1 (not_1_out, Intput1);
  not not_2 (not_2_out, Input_2);
  LED led_1 (.in(and_1_out));
  and and_1 (and_1_out, D, not_2_out, not_1_out);
  LED led_2 (.in(and_2_out));
  and and_2 (and_2_out, D, not_2_out, Intput1);
  and and_3 (and_3_out, D, Input_2, not_1_out);
  LED led_3 (.in(and_3_out));
  LED led_4 (.in(and_4_out));
  and and_4 (and_4_out, D, Input_2, Intput1);

  // Notes on the sheet:
  //   Fixed input
  //   Demultiplexer
endmodule
